// Logisim project Proyecto.circ as structural Verilog: 20 circuits, main circuit main
module main (
  input  w,
  input  x,
  input  y,
  input  z,
  input  w_2,
  input  x_2,
  input  y_2,
  input  z_2
);

  wire Decodificador_2_out_5, Decodificador_2_out_6, Decodificador_2_out_7, Decodificador_2_out_8,
       Decodificador_2_out_9, Decodificador_2_out_10, Decodificador_2_out_11, Decodificador_3_out_5,
       Decodificador_3_out_6, Decodificador_3_out_7, Decodificador_3_out_8, Decodificador_3_out_9,
       Decodificador_3_out_10, Decodificador_3_out_11, Decodificador_Grupo_1_out_5,
       Decodificador_Grupo_1_out_6, Decodificador_Grupo_1_out_7, Decodificador_Grupo_1_out_8,
       Decodificador_Grupo_1_out_9, Decodificador_Grupo_1_out_10, Decodificador_Grupo_1_out_11,
       Decodificador_out_5, Decodificador_out_6, Decodificador_out_7, Decodificador_out_8,
       Decodificador_out_9, Decodificador_out_10, Decodificador_out_11, Sumador_s0, Sumador_s1, Sumador_s2,
       Sumador_s3;

  Decodificador Decodificador (
    .w(w_2), .x(x_2), .y(y_2), .z(z_2), .out_5(Decodificador_out_5), .out_6(Decodificador_out_6),
    .out_7(Decodificador_out_7), .out_8(Decodificador_out_8), .out_9(Decodificador_out_9),
    .out_10(Decodificador_out_10), .out_11(Decodificador_out_11));
  Decodificador Decodificador_2 (
    .w(w), .x(x), .y(y), .z(z), .out_5(Decodificador_2_out_5), .out_6(Decodificador_2_out_6),
    .out_7(Decodificador_2_out_7), .out_8(Decodificador_2_out_8), .out_9(Decodificador_2_out_9),
    .out_10(Decodificador_2_out_10), .out_11(Decodificador_2_out_11));
  _7_Segment_Display u_7_segment_display_1 (
    .g(Decodificador_2_out_11), .f(Decodificador_2_out_10), .a(Decodificador_2_out_5),
    .b(Decodificador_2_out_6), .e(Decodificador_2_out_9), .d(Decodificador_2_out_8), .c(Decodificador_2_out_7));  // open: dp
  _7_Segment_Display u_7_segment_display_2 (
    .g(Decodificador_out_11), .f(Decodificador_out_10), .a(Decodificador_out_5), .b(Decodificador_out_6),
    .e(Decodificador_out_9), .d(Decodificador_out_8), .c(Decodificador_out_7));  // open: dp
  Sumador Sumador (
    .W1(y), .W2(x), .W3(w), .W0(z), .X0(z_2), .X1(y_2), .X2(x_2), .X3(w_2), .S0(Sumador_s0), .S1(Sumador_s1),
    .S2(Sumador_s2), .S3(Sumador_s3));  // open: S4
  Decodificador_Grupo_1 Decodificador_Grupo_1 (
    .w(Sumador_s3), .x(Sumador_s2), .y(Sumador_s1), .z(Sumador_s0), .out_5(Decodificador_Grupo_1_out_5),
    .out_6(Decodificador_Grupo_1_out_6), .out_7(Decodificador_Grupo_1_out_7),
    .out_8(Decodificador_Grupo_1_out_8), .out_9(Decodificador_Grupo_1_out_9),
    .out_10(Decodificador_Grupo_1_out_10), .out_11(Decodificador_Grupo_1_out_11));
  Decodificador Decodificador_3 (
    .w(Sumador_s3), .x(Sumador_s2), .y(Sumador_s1), .z(Sumador_s0), .out_5(Decodificador_3_out_5),
    .out_6(Decodificador_3_out_6), .out_7(Decodificador_3_out_7), .out_8(Decodificador_3_out_8),
    .out_9(Decodificador_3_out_9), .out_10(Decodificador_3_out_10), .out_11(Decodificador_3_out_11));
  _7_Segment_Display u_7_segment_display_3 (
    .g(Decodificador_3_out_11), .f(Decodificador_3_out_10), .a(Decodificador_3_out_5),
    .b(Decodificador_3_out_6), .e(Decodificador_3_out_9), .d(Decodificador_3_out_8), .c(Decodificador_3_out_7));  // open: dp
  _7_Segment_Display u_7_segment_display_4 (
    .g(Decodificador_Grupo_1_out_11), .f(Decodificador_Grupo_1_out_10), .a(Decodificador_Grupo_1_out_5),
    .b(Decodificador_Grupo_1_out_6), .e(Decodificador_Grupo_1_out_9), .d(Decodificador_Grupo_1_out_8),
    .c(Decodificador_Grupo_1_out_7));  // open: dp
endmodule

module Decodificador (
  input  w,
  input  x,
  input  y,
  input  z,
  output out_5,
  output out_6,
  output out_7,
  output out_8,
  output out_9,
  output out_10,
  output out_11
);

  segmento_a_0_9_normal segmento_a_0_9_normal_1 (.w(w), .x(x), .y(y), .z(z), .out_5(out_5));
  segmento_b_0_9_normal segmento_b_0_9_normal_1 (.w(w), .x(x), .y(y), .z(z), .out_5(out_6));
  segmento_c_0_9_normal segmento_c_0_9_normal_1 (.w(w), .x(x), .y(y), .z(z), .out_5(out_7));
  segmento_d_0_9_normal segmento_d_0_9_normal_1 (.w(w), .x(x), .y(y), .z(z), .out_5(out_8));
  segmento_e_0_9_normal segmento_e_0_9_normal_1 (.w(w), .x(x), .y(y), .z(z), .out_5(out_9));
  segmento_f_0_9_normal segmento_f_0_9_normal_1 (.w(w), .x(x), .y(y), .z(z), .out_5(out_10));
  segmento_g_0_9_normal segmento_g_0_9_normal_1 (.w(w), .x(x), .y(y), .z(z), .out_5(out_11));
endmodule

// A
module segmento_a_0_9_normal (
  input  w,
  input  x,
  input  y,
  input  z,
  output out_5
);

  wire not_1_out, not_2_out, not_3_out, not_4_out, or_1_out, or_2_out, w_prime_x_out, w_prime_xz_out,
       w_prime_y_out, wx_prime_out, wx_prime_y_prime_out, x_prime_y_prime_out, x_prime_y_prime_z_prime_out;

  not not_1 (not_1_out, w);
  and w_prime_y (w_prime_y_out, not_1_out, y);
  and w_prime_x (w_prime_x_out, not_1_out, x);
  not not_2 (not_2_out, x);
  and w_prime_xz (w_prime_xz_out, w_prime_x_out, z);
  and wx_prime (wx_prime_out, w, not_2_out);
  not not_3 (not_3_out, y);
  not not_4 (not_4_out, z);
  or or_1 (or_1_out, w_prime_y_out, w_prime_xz_out);
  and wx_prime_y_prime (wx_prime_y_prime_out, wx_prime_out, not_3_out);
  and x_prime_y_prime (x_prime_y_prime_out, not_3_out, not_2_out);
  and x_prime_y_prime_z_prime (x_prime_y_prime_z_prime_out, x_prime_y_prime_out, not_4_out);
  or or_2 (or_2_out, wx_prime_y_prime_out, x_prime_y_prime_z_prime_out);
  or or_3 (out_5, or_1_out, or_2_out);
endmodule

// B
module segmento_b_0_9_normal (
  input  w,
  input  x,
  input  y,
  input  z,
  output out_5
);

  wire not_1_out, not_2_out, not_3_out, not_4_out, or_1_out, or_3_out, w_prime_x_prime_out,
       w_prime_x_prime_y_out, w_prime_y_out, w_prime_y_prime_out, w_prime_y_prime_z_prime_out,
       w_prime_yz_out, x_prime_y_prime_out;

  not not_1 (not_1_out, w);
  not not_2 (not_2_out, x);
  not not_3 (not_3_out, y);
  not not_4 (not_4_out, z);
  and w_prime_y_prime (w_prime_y_prime_out, not_1_out, not_3_out);
  and x_prime_y_prime (x_prime_y_prime_out, not_2_out, not_3_out);
  and w_prime_y_prime_z_prime (w_prime_y_prime_z_prime_out, w_prime_y_prime_out, not_4_out);
  and w_prime_y (w_prime_y_out, y, not_1_out);
  and w_prime_x_prime (w_prime_x_prime_out, not_2_out, not_1_out);
  and w_prime_yz (w_prime_yz_out, w_prime_y_out, z);
  and w_prime_x_prime_y (w_prime_x_prime_y_out, w_prime_x_prime_out, y);
  or or_1 (or_1_out, w_prime_y_prime_z_prime_out, x_prime_y_prime_out);
  or or_2 (out_5, or_1_out, or_3_out);
  or or_3 (or_3_out, w_prime_yz_out, w_prime_x_prime_y_out);
endmodule

// C
module segmento_c_0_9_normal (
  input  w,
  input  x,
  input  y,
  input  z,
  output out_5
);

  wire not_1_out, not_2_out, not_3_out, or_1_out, or_2_out, w_prime_x_out, w_prime_xy_out, w_prime_y_out,
       w_prime_y_prime_out, w_prime_yz_out, x_prime_y_prime_out;

  not not_1 (not_1_out, w);
  not not_2 (not_2_out, x);
  not not_3 (not_3_out, y);
  and w_prime_y_prime (w_prime_y_prime_out, not_1_out, not_3_out);
  and x_prime_y_prime (x_prime_y_prime_out, not_3_out, not_2_out);
  and w_prime_y (w_prime_y_out, not_1_out, y);
  and w_prime_yz (w_prime_yz_out, w_prime_y_out, z);
  and w_prime_x (w_prime_x_out, not_1_out, x);
  or or_1 (or_1_out, w_prime_y_prime_out, x_prime_y_prime_out);
  and w_prime_xy (w_prime_xy_out, w_prime_x_out, y);
  or or_2 (or_2_out, w_prime_yz_out, w_prime_xy_out);
  or or_3 (out_5, or_1_out, or_2_out);
endmodule

// D
module segmento_d_0_9_normal (
  input  w,
  input  x,
  input  y,
  input  z,
  output out_5
);

  wire not_1_out, not_2_out, not_3_out, not_4_out, or_1_out, or_2_out, or_3_out, w_prime_x_out,
       w_prime_x_prime_out, w_prime_x_prime_y_out, w_prime_xy_prime_out, w_prime_xy_prime_z_out,
       w_prime_y_out, w_prime_yz_prime_out, wx_prime_out, wx_prime_y_prime_out, x_prime_y_prime_out,
       x_prime_y_prime_z_prime_out;

  not not_1 (not_1_out, x);
  not not_2 (not_2_out, y);
  not not_3 (not_3_out, z);
  not not_4 (not_4_out, w);
  and wx_prime (wx_prime_out, w, not_1_out);
  and x_prime_y_prime (x_prime_y_prime_out, not_1_out, not_2_out);
  and wx_prime_y_prime (wx_prime_y_prime_out, wx_prime_out, not_2_out);
  and x_prime_y_prime_z_prime (x_prime_y_prime_z_prime_out, x_prime_y_prime_out, not_3_out);
  and w_prime_x_prime (w_prime_x_prime_out, not_1_out, not_4_out);
  and w_prime_x_prime_y (w_prime_x_prime_y_out, w_prime_x_prime_out, y);
  and w_prime_y (w_prime_y_out, not_4_out, y);
  and w_prime_x (w_prime_x_out, not_4_out, x);
  or or_1 (or_1_out, wx_prime_y_prime_out, x_prime_y_prime_z_prime_out);
  and w_prime_yz_prime (w_prime_yz_prime_out, w_prime_y_out, not_3_out);
  and w_prime_xy_prime (w_prime_xy_prime_out, w_prime_x_out, not_2_out);
  or or_2 (or_2_out, w_prime_x_prime_y_out, w_prime_yz_prime_out);
  and w_prime_xy_prime_z (w_prime_xy_prime_z_out, w_prime_xy_prime_out, z);
  or or_3 (or_3_out, or_1_out, or_2_out);
  or or_4 (out_5, or_3_out, w_prime_xy_prime_z_out);
endmodule

// E
module segmento_e_0_9_normal (
  input  w,
  input  x,
  input  y,
  input  z,
  output out_5
);

  wire not_1_out, not_2_out, not_3_out, not_4_out, w_prime_y_out, w_prime_yz_prime_out, x_prime_y_prime_out,
       x_prime_y_prime_z_prime_out;

  not not_1 (not_1_out, w);
  not not_2 (not_2_out, x);
  not not_3 (not_3_out, y);
  not not_4 (not_4_out, z);
  and w_prime_y (w_prime_y_out, not_1_out, y);
  and x_prime_y_prime (x_prime_y_prime_out, not_2_out, not_3_out);
  and x_prime_y_prime_z_prime (x_prime_y_prime_z_prime_out, x_prime_y_prime_out, not_4_out);
  and w_prime_yz_prime (w_prime_yz_prime_out, w_prime_y_out, not_4_out);
  or or_1 (out_5, w_prime_yz_prime_out, x_prime_y_prime_z_prime_out);
endmodule

// F
module segmento_f_0_9_normal (
  input  w,
  input  x,
  input  y,
  input  z,
  output out_5
);

  wire not_1_out, not_2_out, not_3_out, not_4_out, or_1_out, or_2_out, w_prime_x_2_out, w_prime_x_out,
       w_prime_xy_prime_out, w_prime_xz_prime_out, wx_prime_out, wx_prime_y_prime_out, x_prime_y_prime_out,
       x_prime_y_prime_z_prime_out;

  not not_1 (not_1_out, w);
  not not_2 (not_2_out, x);
  not not_3 (not_3_out, y);
  not not_4 (not_4_out, z);
  and w_prime_x (w_prime_x_out, not_1_out, x);
  and w_prime_xy_prime (w_prime_xy_prime_out, w_prime_x_out, not_3_out);
  and x_prime_y_prime (x_prime_y_prime_out, not_2_out, not_3_out);
  and w_prime_x_2 (w_prime_x_2_out, not_1_out, x);
  and x_prime_y_prime_z_prime (x_prime_y_prime_z_prime_out, x_prime_y_prime_out, not_4_out);
  and wx_prime (wx_prime_out, not_2_out, w);
  and wx_prime_y_prime (wx_prime_y_prime_out, wx_prime_out, not_3_out);
  and w_prime_xz_prime (w_prime_xz_prime_out, not_4_out, w_prime_x_2_out);
  or or_1 (or_1_out, w_prime_xy_prime_out, x_prime_y_prime_z_prime_out);
  or or_2 (or_2_out, wx_prime_y_prime_out, w_prime_xz_prime_out);
  or or_3 (out_5, or_1_out, or_2_out);
endmodule

// G
module segmento_g_0_9_normal (
  input  w,
  input  x,
  input  y,
  input  z,
  output out_5
);

  wire not_1_out, not_2_out, not_3_out, not_4_out, or_1_out, or_2_out, w_prime_x_out, w_prime_x_prime_out,
       w_prime_x_prime_y_out, w_prime_xy_prime_out, w_prime_y_out, w_prime_yz_prime_out, wx_prime_out,
       wx_prime_y_prime_out;

  not not_1 (not_1_out, w);
  not not_2 (not_2_out, x);
  not not_3 (not_3_out, y);
  not not_4 (not_4_out, z);
  and w_prime_x (w_prime_x_out, not_1_out, x);
  and w_prime_xy_prime (w_prime_xy_prime_out, w_prime_x_out, not_3_out);
  and w_prime_x_prime (w_prime_x_prime_out, not_1_out, not_2_out);
  and wx_prime (wx_prime_out, not_2_out, w);
  and w_prime_x_prime_y (w_prime_x_prime_y_out, w_prime_x_prime_out, y);
  and w_prime_y (w_prime_y_out, not_1_out, y);
  and wx_prime_y_prime (wx_prime_y_prime_out, wx_prime_out, not_3_out);
  and w_prime_yz_prime (w_prime_yz_prime_out, not_4_out, w_prime_y_out);
  or or_1 (or_1_out, w_prime_xy_prime_out, wx_prime_y_prime_out);
  or or_2 (or_2_out, w_prime_x_prime_y_out, w_prime_yz_prime_out);
  or or_3 (out_5, or_1_out, or_2_out);
endmodule

module Medio_Sumador (
  input  w,
  input  x,
  output S,
  output Count
);

  wire and_1_out, and_2_out, not_1_out, not_2_out;

  not not_1 (not_1_out, w);
  not not_2 (not_2_out, x);
  and and_1 (and_1_out, not_1_out, x);
  and and_2 (and_2_out, not_2_out, w);
  or \xor  (S, and_1_out, and_2_out);
  and and_3 (Count, w, x);
endmodule

// FA
module Sumador_Completo (
  input  W,
  input  X,
  input  Count,
  output S,
  output Count_2
);

  wire medio_sumador_1_count, medio_sumador_1_s, medio_sumador_2_count;

  Medio_Sumador medio_sumador_1 (.w(W), .x(X), .S(medio_sumador_1_s), .Count(medio_sumador_1_count));
  Medio_Sumador medio_sumador_2 (.w(Count), .x(medio_sumador_1_s), .S(S), .Count(medio_sumador_2_count));
  or or_1 (Count_2, medio_sumador_2_count, medio_sumador_1_count);
endmodule

module Sumador (
  input  W1,
  input  W2,
  input  W3,
  input  W0,
  input  X0,
  input  X1,
  input  X2,
  input  X3,
  output S0,
  output S1,
  output S2,
  output S3,
  output S4
);

  wire sumador_completo_1_count_2, sumador_completo_2_count_2, sumador_completo_3_count_2;

  Sumador_Completo sumador_completo_1 (.W(W0), .X(X0), .Count(1'b0), .S(S0), .Count_2(sumador_completo_1_count_2));
  Sumador_Completo sumador_completo_2 (
    .W(W1), .X(X1), .Count(sumador_completo_1_count_2), .S(S1), .Count_2(sumador_completo_2_count_2));
  Sumador_Completo sumador_completo_3 (
    .W(W2), .X(X2), .Count(sumador_completo_2_count_2), .S(S2), .Count_2(sumador_completo_3_count_2));
  Sumador_Completo sumador_completo_4 (.W(W3), .X(X3), .Count(sumador_completo_3_count_2), .S(S3), .Count_2(S4));
endmodule

module Decodificador_Grupo_1 (
  input  w,
  input  x,
  input  y,
  input  z,
  output out_5,
  output out_6,
  output out_7,
  output out_8,
  output out_9,
  output out_10,
  output out_11
);

  segmento_a_0_9_Grupo_1 segmento_a_0_9_grupo_1_1 (.w(w), .x(x), .y(y), .z(z), .out_5(out_5));
  segmento_b_0_9_Grupo_1 segmento_b_0_9_grupo_1_1 (.w(w), .x(x), .y(y), .z(z), .out_5(out_6));
  segmento_c_0_9_Grupo_1 segmento_c_0_9_grupo_1_1 (.w(w), .x(x), .y(y), .z(z), .out_5(out_7));
  segmento_d_0_9_Grupo_1 segmento_d_0_9_grupo_1_1 (.w(w), .x(x), .y(y), .z(z), .out_5(out_8));
  segmento_e_0_9_Grupo_1 segmento_e_0_9_grupo_1_1 (.w(w), .x(x), .y(y), .z(z), .out_5(out_9));
  segmento_f_0_9_Grupo_1 segmento_f_0_9_grupo_1_1 (.w(w), .x(x), .y(y), .z(z), .out_5(out_10));
  segmento_g_0_9_Grupo_1 segmento_g_0_9_grupo_1_1 (.w(w), .x(x), .y(y), .z(z), .out_5(out_11));
endmodule

// A
module segmento_a_0_9_Grupo_1 (
  input  w,
  input  x,
  input  y,
  input  z,
  output out_5
);

  wire not_1_out, not_2_out, not_3_out, or_1_out, or_2_out, or_3_out, wy_out, wy_prime_out, wy_prime_z_out,
       wyz_prime_out, x_prime_y_prime_out, x_prime_z_prime_out, xy_out, xyz_out;

  not not_1 (not_1_out, x);
  not not_2 (not_2_out, y);
  not not_3 (not_3_out, z);
  and xy (xy_out, x, y);
  and xyz (xyz_out, xy_out, z);
  and x_prime_y_prime (x_prime_y_prime_out, not_1_out, not_2_out);
  and x_prime_z_prime (x_prime_z_prime_out, not_1_out, not_3_out);
  and wy_prime (wy_prime_out, w, not_2_out);
  and wy (wy_out, w, y);
  and wy_prime_z (wy_prime_z_out, wy_prime_out, z);
  and wyz_prime (wyz_prime_out, wy_out, not_3_out);
  or or_1 (or_1_out, x_prime_y_prime_out, x_prime_z_prime_out);
  or or_2 (or_2_out, wy_prime_z_out, wyz_prime_out);
  or or_3 (or_3_out, or_1_out, or_2_out);
  or or_4 (out_5, xyz_out, or_3_out);
endmodule

// B
module segmento_b_0_9_Grupo_1 (
  input  w,
  input  x,
  input  y,
  input  z,
  output out_5
);

  wire not_1_out, not_2_out, not_3_out, not_4_out, or_1_out, or_2_out, w_prime_y_out, w_prime_yz_out,
       wx_prime_out, wx_prime_z_prime_out, xy_prime_out, xz_out;

  not not_1 (not_1_out, w);
  not not_2 (not_2_out, x);
  not not_3 (not_3_out, y);
  not not_4 (not_4_out, z);
  and w_prime_y (w_prime_y_out, not_1_out, y);
  and xy_prime (xy_prime_out, x, not_3_out);
  and xz (xz_out, x, z);
  and wx_prime (wx_prime_out, w, not_2_out);
  and w_prime_yz (w_prime_yz_out, w_prime_y_out, z);
  and wx_prime_z_prime (wx_prime_z_prime_out, wx_prime_out, not_4_out);
  or or_1 (or_1_out, xy_prime_out, xz_out);
  or or_2 (or_2_out, w_prime_yz_out, wx_prime_z_prime_out);
  or or_3 (out_5, or_1_out, or_2_out);
endmodule

// C
module segmento_c_0_9_Grupo_1 (
  input  w,
  input  x,
  input  y,
  input  z,
  output out_5
);

  wire not_1_out, not_2_out, not_3_out, not_4_out, or_1_out, or_2_out, or_3_out, w_prime_x_out,
       w_prime_xy_prime_out, wx_prime_out, wx_prime_z_out, x_prime_y_out, xy_prime_out, xy_prime_z_prime_out,
       yz_out;

  not not_1 (not_1_out, w);
  not not_2 (not_2_out, x);
  not not_3 (not_3_out, y);
  not not_4 (not_4_out, z);
  and w_prime_x (w_prime_x_out, not_1_out, x);
  and yz (yz_out, y, z);
  and xy_prime (xy_prime_out, x, not_3_out);
  and wx_prime (wx_prime_out, w, not_2_out);
  and w_prime_xy_prime (w_prime_xy_prime_out, w_prime_x_out, not_3_out);
  and x_prime_y (x_prime_y_out, not_2_out, y);
  and xy_prime_z_prime (xy_prime_z_prime_out, not_4_out, xy_prime_out);
  and wx_prime_z (wx_prime_z_out, wx_prime_out, z);
  or or_1 (or_1_out, x_prime_y_out, yz_out);
  or or_2 (or_2_out, xy_prime_z_prime_out, wx_prime_z_out);
  or or_3 (or_3_out, or_1_out, or_2_out);
  or or_4 (out_5, w_prime_xy_prime_out, or_3_out);
endmodule

// D
module segmento_d_0_9_Grupo_1 (
  input  w,
  input  x,
  input  y,
  input  z,
  output out_5
);

  wire not_1_out, not_2_out, not_3_out, not_4_out, or_1_out, or_2_out, or_3_out, or_4_out, w_prime_x_out,
       w_prime_x_prime_out, w_prime_x_prime_z_prime_out, w_prime_xy_out, wx_out, wx_prime_out,
       wx_prime_y_out, wxy_prime_out, wz_out, xz_out;

  not not_1 (not_1_out, w);
  not not_2 (not_2_out, x);
  not not_3 (not_3_out, y);
  not not_4 (not_4_out, z);
  and w_prime_x_prime (w_prime_x_prime_out, not_1_out, not_2_out);
  and wx (wx_out, w, x);
  and wx_prime (wx_prime_out, w, not_2_out);
  and w_prime_x (w_prime_x_out, not_1_out, x);
  and w_prime_x_prime_z_prime (w_prime_x_prime_z_prime_out, w_prime_x_prime_out, not_4_out);
  and wxy_prime (wxy_prime_out, wx_out, not_3_out);
  and wx_prime_y (wx_prime_y_out, wx_prime_out, y);
  and w_prime_xy (w_prime_xy_out, w_prime_x_out, y);
  and wz (wz_out, w, z);
  and xz (xz_out, x, z);
  or or_1 (or_1_out, w_prime_x_prime_z_prime_out, wxy_prime_out);
  or or_2 (or_2_out, wx_prime_y_out, w_prime_xy_out);
  or or_3 (or_3_out, wz_out, xz_out);
  or or_4 (or_4_out, or_1_out, or_2_out);
  or or_5 (out_5, or_4_out, or_3_out);
endmodule

// E
module segmento_e_0_9_Grupo_1 (
  input  w,
  input  x,
  input  y,
  input  z,
  output out_5
);

  wire not_1_out, not_2_out, not_3_out, not_4_out, or_1_out, or_2_out, or_3_out, or_4_out,
       w_prime_x_prime_out, w_prime_y_out, wz_out, wz_prime_out, x_prime_y_out, xy_prime_out, xy_prime_z_out;

  not not_1 (not_1_out, w);
  not not_2 (not_2_out, x);
  not not_3 (not_3_out, y);
  not not_4 (not_4_out, z);
  and w_prime_x_prime (w_prime_x_prime_out, not_1_out, not_2_out);
  and xy_prime (xy_prime_out, x, not_3_out);
  and wz_prime (wz_prime_out, w, not_4_out);
  and x_prime_y (x_prime_y_out, not_2_out, y);
  and w_prime_y (w_prime_y_out, not_1_out, y);
  and wz (wz_out, not_1_out, z);
  and xy_prime_z (xy_prime_z_out, xy_prime_out, z);
  or or_1 (or_1_out, w_prime_x_prime_out, xy_prime_z_out);
  or or_2 (or_2_out, wz_prime_out, x_prime_y_out);
  or or_3 (or_3_out, w_prime_y_out, wz_out);
  or or_4 (or_4_out, or_1_out, or_2_out);
  or or_5 (out_5, or_4_out, or_3_out);
endmodule

// F
module segmento_f_0_9_Grupo_1 (
  input  w,
  input  x,
  input  y,
  input  z,
  output out_5
);

  wire not_1_out, not_2_out, not_3_out, or_1_out, or_2_out, or_3_out, w_prime_x_prime_out, wz_out,
       x_prime_y_prime_out, xy_out, yz_out;

  not not_1 (not_1_out, w);
  not not_2 (not_2_out, x);
  not not_3 (not_3_out, y);
  // NOT_Gate not_4 has open pins: in=z, out=open
  and w_prime_x_prime (w_prime_x_prime_out, not_1_out, not_2_out);
  and x_prime_y_prime (x_prime_y_prime_out, not_2_out, not_3_out);
  and wz (wz_out, w, z);
  and xy (xy_out, x, y);
  and yz (yz_out, y, z);
  or or_1 (or_1_out, w_prime_x_prime_out, x_prime_y_prime_out);
  or or_2 (or_2_out, wz_out, xy_out);
  or or_3 (or_3_out, or_1_out, or_2_out);
  or or_4 (out_5, or_3_out, yz_out);
endmodule

// G
module segmento_g_0_9_Grupo_1 (
  input  w,
  input  x,
  input  y,
  input  z,
  output out_5
);

  wire not_1_out;

  not not_1 (not_1_out, x);
  or w_x_prime (out_5, w, not_1_out);
endmodule
